# Fritzing sketch circuit (saved by Fritzing 0.9.1b)
breadboards: 1

parts:
  Raspberry_Pi1 = Raspberry Pi B+
  Power_plug1 = Power plug
  IC1 = Hex Inverter Schmitt Trigger SN74HC14 [package="DIP (Dual Inline)"]
  S1 = Pushbutton [package="[THT]"]
  S2 = Pushbutton [package="[THT]"]
  RPR-220 = QRD1114 [package=qrd1114]
  R3 = Resistor [tolerance=±5% resistance=10k package=THT]
  R4 = Resistor [tolerance=±5% resistance=10k package=THT]
  Part1 = AE-MOTOR8830 - DRV8830 Breakout [part_number=drv8830]
  U2 = AKIZUKI-PCA9306 [package=psop-8]
  R5 = Resistor [tolerance=±5% resistance=100 package=THT]
  M1 = DC Motor

nets:
  3V3: Raspberry_Pi1.3v3, Raspberry_Pi1.3V3, IC1.VCC, S2.Pin_1, S2.Pin_2, RPR-220.E, U2.VREF2, R5.Pin_0
  N1: Raspberry_Pi1.GPIO2, U2.SDA2
  N2: Raspberry_Pi1.GPIO3, U2.SCL2
  N3: Raspberry_Pi1.GPIO17, IC1.5Y
  GND: Raspberry_Pi1.GND, Power_plug1.GND, IC1.GND, RPR-220.K, R3.Pin_0, R4.Pin_0, Part1.GND, U2.GND
  N4: Raspberry_Pi1.GPIO18, IC1.6Y
  VCC: Raspberry_Pi1.5V, Power_plug1.VCC, Part1.VCC, U2.VREF1
  N5: IC1.5A, S1.Pin_3, S1.Pin_4, R4.Pin_1
  N6: IC1.6A, RPR-220.C, R3.Pin_1
  N7: S1.Pin_1, S1.Pin_2, S2.Pin_3, S2.Pin_4
  N8: RPR-220.A, R5.Pin_1
  N9: Part1.SCL, U2.SCL1
  N10: Part1.SDA, U2.SDA1
  N11: Part1.OUT1, M1.pin_1
  N12: Part1.OUT2, M1.pin_2

notes:
  K C E A

custom parts:
  AKIZUKI-PCA9306: Bidirectional I2C level shifter. NOT compatible with all available part number pinout schemes- DOUBLE CHECK!!!
